// Logisim project ALU.circ as structural Verilog: 1 circuit, main circuit ALU
module ALU (
  input  [31:0] A,
  input  [31:0] B,
  input  [4:0] Shift,
  input  [3:0] Codop,
  input  CarryIn,
  output [31:0] S,
  output [3:0] Flags
);

  wire CInBarre;
  wire [31:0] AandB, AfoisB, AorB, AplusB, AplusBplusCIn, ASR, AxorB, BandNotA, BmoinsA, BmoinsAplusCInBarre,
       LSL, LSR, not_1_out, not_2_out, notA, rotR, zero, ZeromoinsA;

  assign AandB = A & B;  // AND_Gate AandB, 32 bits wide
  assign AxorB = A ^ B;  // XOR_Gate AxorB, 32 bits wide
  Adder #(.width(32)) adder_1 (.a(A), .b(B), .out(AplusB));  // open: cin, cout
  Subtractor #(.width(32)) subtractor_1 (.a(B), .b(A), .out(BmoinsA));  // open: bin, bout
  Adder #(.width(32)) adder_2 (.a(A), .b(B), .out(AplusBplusCIn), .cin(CarryIn));  // open: cout
  Adder #(.width(32)) adder_3 (.a(BmoinsA), .out(BmoinsAplusCInBarre), .cin(CInBarre));  // open: b, cout
  Negator #(.width(1)) negator_1 (.in(CarryIn), .out(CInBarre));
  Subtractor #(.width(32)) subtractor_2 (.a(zero), .b(A), .out(ZeromoinsA));  // open: bin, bout
  Multiplier #(.width(32)) multiplier_1 (.a(A), .b(B), .out(AfoisB));  // open: cin, cout
  assign not_1_out = ~A;  // NOT_Gate not_1, 32 bits wide
  assign zero = A & not_1_out;  // AND_Gate ZERO, 32 bits wide
  assign not_2_out = ~A;  // NOT_Gate not_2, 32 bits wide
  assign BandNotA = not_2_out & B;  // AND_Gate BandNotA, 32 bits wide
  assign notA = ~A;  // NOT_Gate not_3, 32 bits wide
  assign AorB = A | B;  // OR_Gate AorB, 32 bits wide
  Multiplexer #(.select(4), .width(32)) multiplexer_1 (
    .in0(AandB), .in1(AxorB), .in2(LSL), .in3(LSR), .in4(ASR), .in5(AplusBplusCIn),
    .in6(BmoinsAplusCInBarre), .in7(rotR), .in8(AandB), .in9(ZeromoinsA), .in10(BmoinsA), .in11(AplusB),
    .in12(AorB), .in13(AfoisB), .in14(BandNotA), .in15(notA), .out(S), .sel(Codop));
  Shifter #(.width(32)) shifter_1 (.in(B), .\dist (Shift), .out(LSL));
  Shifter #(.shift("lr"), .width(32)) shifter_2 (.in(B), .\dist (Shift), .out(LSR));
  Shifter #(.shift("ar"), .width(32)) shifter_3 (.in(B), .\dist (Shift), .out(ASR));
  Shifter #(.shift("rr"), .width(32)) shifter_4 (.in(B), .\dist (Shift), .out(rotR));

  // Other names for the same wires on the sheet: CIn = CarryIn; F[3:0] = Flags

  // Notes on the sheet:
  //   Note: for ROR, C = N
  //   Note 2: assume that shift > 0 for LSL and LSR
endmodule
