// Logisim project Ctl_Data_Processing.circ as structural Verilog: 1 circuit, main circuit Data_Processing
module Data_Processing (
  input  Enable,
  input  [15:0] Instruction,
  output [2:0] Rd,
  output [2:0] Rn,
  output [2:0] Rm,
  output [3:0] ALU_Opcode,
  output [3:0] Flags_Update_Mask
);

  wire [3:1] E;

  Multiplexer multiplexer_1 ();  // open: in0, in1, out, sel
  assign ALU_Opcode = {E, Enable} & Instruction[9:6];  // AND_Gate and_1, 4 bits wide
  // Pins of 1 and 4 bits meet at {E, Enable}

  // Other names for the same wires on the sheet: E[0] = Enable; ALU[3:0] = Instruction[9:6]

  // Notes on the sheet:
  //   Note 2: RSB instruction has Rn as 1st operand.
  //   MUL instruction has Rn as 1st operand and Rdm as 2nd operand
  //   For simplification purposes, Rm is used for 1st operand both here and in the ALU.
  //   Note: instructions that does not save the result will still have the second operand as the destination register, the ALU will copy the second register to the destination register
  //   Pull output low on Enable = 0
endmodule
